// Logisim project Аоис4_2.circ as structural Verilog: 1 circuit, main circuit main
module main (
  input  [3:0] in_1,
  output [3:0] out_2,
  output [3:0] out_3,
  output [3:0] out_4
);

  wire and_1_out, not_2_out, or_1_out;

  not not_1 (out_2[0], in_1[0]);
  xor xor_1 (out_2[1], in_1[0], in_1[1]);
  and and_1 (and_1_out, in_1[0], in_1[1]);
  not not_2 (not_2_out, in_1[2]);
  or or_1 (or_1_out, in_1[0], in_1[1]);
  xor xor_2 (out_2[2], in_1[2], and_1_out);
  and and_2 (out_2[3], in_1[3], not_2_out, or_1_out);

  assign out_3 = in_1;
  assign out_4 = out_2;

  // Notes on the sheet:
  //   Y0
  //   Y1
  //   Y2
  //   Y3
endmodule
